// Digital circuit 4-Bit-Counter.dig as structural Verilog
module _4_Bit_Counter (
  input  R,
  input  CE,
  input  clk,
  input  D4,
  input  D3,
  input  D2,
  input  D1,
  input  L,
  output rout,
  output Q1,
  output Q2,
  output Q3,
  output Q4
);

  wire and_1_out, and_2_out, and_3_out, and_4_out, and_5_out, and_6_out, and_7_out, and_8_out,
       half_adder_1_cout, half_adder_1_sum, half_adder_2_cout, half_adder_2_sum, half_adder_3_cout,
       half_adder_3_sum, half_adder_4_cout, half_adder_4_sum, not_1_out, or_1_out, or_2_out, or_3_out,
       or_4_out, or_5_out;

  not not_1 (not_1_out, L);
  D_flipflop_rising d_flipflop_rising_1 (.c(clk), .D(half_adder_1_cout), .R(R), .Q(rout));  // open: Q_2
  Half_Adder half_adder_1 (.a(Q4), .b(half_adder_2_cout), .cout(half_adder_1_cout), .sum(half_adder_1_sum));
  Half_Adder half_adder_2 (.a(Q3), .b(half_adder_3_cout), .cout(half_adder_2_cout), .sum(half_adder_2_sum));
  Half_Adder half_adder_3 (.a(Q2), .b(half_adder_4_cout), .cout(half_adder_3_cout), .sum(half_adder_3_sum));
  and and_1 (and_1_out, not_1_out, half_adder_1_sum);
  and and_2 (and_2_out, not_1_out, half_adder_2_sum);
  and and_3 (and_3_out, not_1_out, half_adder_3_sum);
  and and_4 (and_4_out, not_1_out, half_adder_4_sum);
  or or_1 (or_1_out, L, CE);
  Half_Adder half_adder_4 (.a(Q1), .b(1'b1), .cout(half_adder_4_cout), .sum(half_adder_4_sum));
  or or_2 (or_2_out, and_8_out, and_1_out);
  or or_3 (or_3_out, and_6_out, and_3_out);
  or or_4 (or_4_out, and_7_out, and_2_out);
  _4_Bit_Register plus_1 (
    .load(or_1_out), .c(clk), .R(R), .D1(or_5_out), .D2(or_3_out), .D3(or_4_out), .D4(or_2_out), .Q1(Q1),
    .Q2(Q2), .Q3(Q3), .Q4(Q4));
  or or_5 (or_5_out, and_5_out, and_4_out);
  and and_5 (and_5_out, D1, L);
  and and_6 (and_6_out, D2, L);
  and and_7 (and_7_out, D3, L);
  and and_8 (and_8_out, D4, L);
  PullDown pulldown_1 ();  // open: out
  PullDown pulldown_2 ();  // open: out
  PullDown pulldown_3 ();  // open: out
  PullDown pulldown_4 ();  // open: out

  // Notes on the sheet:
  //   CE: Loads D into internal register
endmodule
