// Digital circuit 4-Bit-Register.dig as structural Verilog
module _4_Bit_Register (
  input  load,
  input  D4,
  input  c,
  input  R,
  input  D3,
  input  D2,
  input  D1,
  output Q4,
  output Q3,
  output Q2,
  output Q1
);

  PullUp pullup_1 ();  // open: out
  PullUp pullup_2 ();  // open: out
  PullUp pullup_3 ();  // open: out
  PullUp pullup_4 ();  // open: out
  Bit bit_1 (.load(load), .enable(1'b1), .D(D1), .c(c), .R(R), .Q(Q1));
  Bit bit_2 (.load(load), .enable(1'b1), .D(D2), .c(c), .R(R), .Q(Q2));
  Bit bit_3 (.load(load), .enable(1'b1), .D(D3), .c(c), .R(R), .Q(Q3));
  Bit bit_4 (.load(load), .enable(1'b1), .D(D4), .c(c), .R(R), .Q(Q4));

  // Notes on the sheet:
  //   load: pin 5
  //   D4: pin 4
  //   c: pin 7
  //   R: pin 8
  //   D3: pin 3
  //   D2: pin 2
  //   D1: pin 1
endmodule
