// Digital circuit 4-bit-adder.dig as structural Verilog
module _4_bit_adder (
  input  A1,
  input  A2,
  input  A3,
  input  A4,
  input  B1,
  input  B2,
  input  B3,
  input  B4,
  input  cin,
  output Y1,
  output Y2,
  output Y3,
  output Y4,
  output cout
);

  wire full_adder_1_cout, full_adder_2_cout, full_adder_3_cout;

  Full_Adder full_adder_1 (.a(A1), .b(B1), .cin(cin), .cout(full_adder_1_cout), .sum(Y1));
  Full_Adder full_adder_2 (.a(A2), .b(B2), .cin(full_adder_1_cout), .cout(full_adder_2_cout), .sum(Y2));
  Full_Adder full_adder_3 (.a(A3), .b(B3), .cin(full_adder_2_cout), .cout(full_adder_3_cout), .sum(Y3));
  Full_Adder full_adder_4 (.a(A4), .b(B4), .cin(full_adder_3_cout), .cout(cout), .sum(Y4));
endmodule
