// Digital circuit 4-bit-simple-counter.dig as structural Verilog
module _4_bit_simple_counter (
  input  R,
  input  CE,
  input  clk,
  output rout,
  output Q1,
  output Q2,
  output Q3,
  output Q4
);

  wire half_adder_1_cout, half_adder_1_sum, half_adder_2_cout, half_adder_2_sum, half_adder_3_cout,
       half_adder_3_sum, half_adder_4_cout, half_adder_4_sum;

  Half_Adder half_adder_1 (.a(Q1), .b(1'b1), .cout(half_adder_1_cout), .sum(half_adder_1_sum));
  Half_Adder half_adder_2 (.a(Q2), .b(half_adder_1_cout), .cout(half_adder_2_cout), .sum(half_adder_2_sum));
  Half_Adder half_adder_3 (.a(Q3), .b(half_adder_2_cout), .cout(half_adder_3_cout), .sum(half_adder_3_sum));
  Half_Adder half_adder_4 (.a(Q4), .b(half_adder_3_cout), .cout(half_adder_4_cout), .sum(half_adder_4_sum));
  D_flipflop_rising d_flipflop_rising_1 (.c(clk), .D(half_adder_4_cout), .R(R), .Q(rout));  // open: Q_2
  // _4_Bit_Register plus_1: pin names not known; wires that end beside it: R, clk, CE, Q2, half_adder_1_sum, half_adder_2_sum, Q3, half_adder_3_sum, half_adder_4_sum, Q4

  // Notes on the sheet:
  //   CE: Loads D into internal register
endmodule
