// Digital circuit 4-bitshift.dig as structural Verilog
module _4_bitshift (
  input  R,
  input  c,
  input  D,
  output Q2,
  output Q1,
  output Q3,
  output Q4
);

  D_flipflop_rising d_flipflop_rising_1 (.c(c), .D(Q3), .R(R), .Q(Q4));  // open: Q_2
  D_flipflop_rising d_flipflop_rising_2 (.c(c), .D(Q2), .R(R), .Q(Q3));  // open: Q_2
  D_flipflop_rising d_flipflop_rising_3 (.c(c), .D(Q1), .R(R), .Q(Q2));  // open: Q_2
  D_flipflop_rising d_flipflop_rising_4 (.c(c), .D(D), .R(R), .Q(Q1));  // open: Q_2
endmodule
