// Digital circuit 4x2mux.dig as structural Verilog
module _4x2mux (
  input  A1,
  input  A2,
  input  A3,
  input  A4,
  input  B1,
  input  B2,
  input  B3,
  input  B4,
  input  sel,
  output Y1,
  output Y2,
  output Y3,
  output Y4
);

  PullDown pulldown_1 ();  // open: out
  PullDown pulldown_2 ();  // open: out
  PullDown pulldown_3 ();  // open: out
  PullDown pulldown_4 ();  // open: out
  mux mux_1 (.a(A4), .b(B4), .sel(sel), .Y(Y4));
  PullDown pulldown_5 ();  // open: out
  mux mux_2 (.a(A3), .b(B3), .sel(sel), .Y(Y3));
  PullDown pulldown_6 ();  // open: out
  mux mux_3 (.a(A2), .b(B2), .sel(sel), .Y(Y2));
  PullDown pulldown_7 ();  // open: out
  mux mux_4 (.a(A1), .b(B1), .sel(sel), .Y(Y1));
  PullDown pulldown_8 ();  // open: out
  PullDown pulldown_9 ();  // open: out
endmodule
