// Digital circuit 7seg-driver.dig as structural Verilog
module _7seg_driver (
  input  D4,
  input  D3,
  input  D2,
  input  D1,
  output t1,
  output t2,
  output t3,
  output u1,
  output u2,
  output u3,
  output u4
);

  wire _0, _1, _2, _3, _4, _5, _6, _7, _8, _9, A, B, C, D, E, F;

  _4_Bit_Dec _4_bit_dec_1 (
    .D4(D4), .D3(D3), .D2(D2), .D1(D1), ._0(_0), ._1(_1), ._2(_2), ._3(_3), ._4(_4), ._5(_5), ._6(_6),
    ._7(_7), ._8(_8), ._9(_9), ._10(A), ._11(B), ._12(C), ._13(D), ._14(E), ._15(F));
  or or_1 (t1, _8, C, A, _2, _0, D, _1, _6, B, E, F);
  or or_2 (t2, _9, C, A, _6, _4, _0, _1, _5, _8, B, E, F);
  or or_3 (u1, F, E, _9, _7, _5, _2, _0, _3, _6, _8, C, A);
  or or_4 (u2, _9, _8, _4, _2, D, _0, _3, _7, A);
  or or_5 (t3, _9, F, A, _4, _2, _6, _5, _3, _8, B, E, D);
  or or_6 (u3, D, B, _9, _7, _5, _3, _0, _4, _6, _9, A, _8);
  or or_7 (u4, D, C, _8, _5, _2, _0, _3, _6, E, B);
endmodule
