// Digital circuit 8-bit-adder.dig as structural Verilog
module _8_bit_adder (
  input  A1,
  input  A2,
  input  A3,
  input  A4,
  input  A5,
  input  A6,
  input  A7,
  input  A8,
  input  B1,
  input  B2,
  input  B3,
  input  B4,
  input  B5,
  input  B6,
  input  B7,
  input  B8,
  input  cin,
  output Y1,
  output Y2,
  output Y3,
  output Y4,
  output Y5,
  output Y6,
  output Y7,
  output Y8,
  output cout
);

  wire _4_bit_adder_2_cout;

  _4_bit_adder _4_bit_adder_1 (
    .A1(A5), .A2(A6), .A3(A7), .A4(A8), .B1(B5), .B2(B6), .B3(B7), .B4(B8), .cin(_4_bit_adder_2_cout),
    .Y1(Y5), .Y2(Y6), .Y3(Y7), .Y4(Y8), .cout(cout));
  _4_bit_adder _4_bit_adder_2 (
    .A1(A1), .A2(A2), .A3(A3), .A4(A4), .B1(B1), .B2(B2), .B3(B3), .B4(B4), .cin(cin), .Y1(Y1), .Y2(Y2),
    .Y3(Y3), .Y4(Y4), .cout(_4_bit_adder_2_cout));
endmodule
