// Digital circuit 8-bit-register.dig as structural Verilog
module _8_bit_register (
  input  D1,
  input  D2,
  input  D3,
  input  D4,
  input  D5,
  input  D6,
  input  D7,
  input  D8,
  input  c,
  input  R,
  input  l,
  output Q1,
  output Q2,
  output Q3,
  output Q4,
  output Q5,
  output Q6,
  output Q7,
  output Q8
);

  _4_Bit_Register _4_bit_register_1 (
    .load(l), .c(c), .R(R), .D1(D1), .D2(D2), .D3(D3), .D4(D4), .Q1(Q1), .Q2(Q2), .Q3(Q3), .Q4(Q4));
  _4_Bit_Register _4_bit_register_2 (
    .load(l), .c(c), .R(R), .D1(D5), .D2(D6), .D3(D7), .D4(D8), .Q1(Q5), .Q2(Q6), .Q3(Q7), .Q4(Q8));
endmodule
