// Digital circuit 8-bitAND.dig as structural Verilog
module _8_bitAND (
  input  A1,
  input  A2,
  input  A3,
  input  A4,
  input  A5,
  input  A6,
  input  A7,
  input  A8,
  input  B1,
  input  B2,
  input  B3,
  input  B4,
  input  B5,
  input  B6,
  input  B7,
  input  B8,
  output Y1,
  output Y2,
  output Y3,
  output Y4,
  output Y5,
  output Y6,
  output Y7,
  output Y8
);

  and and_1 (Y1, B1, A1);
  and and_2 (Y2, B2, A2);
  and and_3 (Y3, B3, A3);
  and and_4 (Y4, B4, A4);
  and and_5 (Y5, B5, A5);
  and and_6 (Y6, B6, A6);
  and and_7 (Y7, B7, A7);
  and and_8 (Y8, B8, A8);
endmodule
