// Digital circuit 8x2mux.dig as structural Verilog
module _8x2mux (
  input  A1,
  input  A2,
  input  A3,
  input  A4,
  input  A5,
  input  A6,
  input  A7,
  input  A8,
  input  B1,
  input  B2,
  input  B3,
  input  B4,
  input  B5,
  input  B6,
  input  B7,
  input  B8,
  input  sel,
  output Y1,
  output Y2,
  output Y3,
  output Y4,
  output Y5,
  output Y6,
  output Y7,
  output Y8
);

  _4x2mux _4x2mux_1 (
    .A1(A1), .A2(A2), .A3(A3), .A4(A4), .B1(B1), .B2(B2), .B3(B3), .B4(B4), .sel(sel), .Y1(Y1), .Y2(Y2),
    .Y3(Y3), .Y4(Y4));
  _4x2mux _4x2mux_2 (
    .A1(A5), .A2(A6), .A3(A7), .A4(A8), .B1(B5), .B2(B6), .B3(B7), .B4(B8), .sel(sel), .Y1(Y5), .Y2(Y6),
    .Y3(Y7), .Y4(Y8));
endmodule
