// Digital circuit ALU.dig as structural Verilog
module ALU (
  input  NA,
  input  NB,
  input  ZA,
  input  ZB,
  input  F,
  input  NO,
  input  A1,
  input  A2,
  input  A3,
  input  A4,
  input  A5,
  input  A6,
  input  A7,
  input  A8,
  input  B1,
  input  B2,
  input  B3,
  input  B4,
  input  B5,
  input  B6,
  input  B7,
  input  B8,
  output of,
  output Y1,
  output Y2,
  output Y3,
  output Y4,
  output Y5,
  output Y6,
  output Y7,
  output Y8,
  output lz,
  output z
);

  wire _8_bit_adder_1_y1, _8_bit_adder_1_y2, _8_bit_adder_1_y3, _8_bit_adder_1_y4, _8_bit_adder_1_y5,
       _8_bit_adder_1_y6, _8_bit_adder_1_y7, _8_bit_adder_1_y8, _8_bitand_1_y1, _8_bitand_1_y2,
       _8_bitand_1_y3, _8_bitand_1_y4, _8_bitand_1_y5, _8_bitand_1_y6, _8_bitand_1_y7, _8_bitand_1_y8,
       _8_bitand_2_y1, _8_bitand_2_y2, _8_bitand_2_y3, _8_bitand_2_y4, _8_bitand_2_y5, _8_bitand_2_y6,
       _8_bitand_2_y7, _8_bitand_2_y8, _8_bitand_3_y1, _8_bitand_3_y2, _8_bitand_3_y3, _8_bitand_3_y4,
       _8_bitand_3_y5, _8_bitand_3_y6, _8_bitand_3_y7, _8_bitand_3_y8, _8_bitxor_1_y1, _8_bitxor_1_y2,
       _8_bitxor_1_y3, _8_bitxor_1_y4, _8_bitxor_1_y5, _8_bitxor_1_y6, _8_bitxor_1_y7, _8_bitxor_1_y8,
       _8_bitxor_2_y1, _8_bitxor_2_y2, _8_bitxor_2_y3, _8_bitxor_2_y4, _8_bitxor_2_y5, _8_bitxor_2_y6,
       _8_bitxor_2_y7, _8_bitxor_2_y8, _8x2mux_1_y1, _8x2mux_1_y2, _8x2mux_1_y3, _8x2mux_1_y4, _8x2mux_1_y5,
       _8x2mux_1_y6, _8x2mux_1_y7, _8x2mux_1_y8, not_1_out, not_2_out;

  not not_1 (not_1_out, ZA);
  not not_2 (not_2_out, ZB);
  _8_bitAND _8_bitand_1 (
    .A1(A1), .A2(A2), .A3(A3), .A4(A4), .A5(A5), .A6(A6), .A7(A7), .A8(A8), .B1(not_1_out), .B2(not_1_out),
    .B3(not_1_out), .B4(not_1_out), .B5(not_1_out), .B6(not_1_out), .B7(not_1_out), .B8(not_1_out),
    .Y1(_8_bitand_1_y1), .Y2(_8_bitand_1_y2), .Y3(_8_bitand_1_y3), .Y4(_8_bitand_1_y4), .Y5(_8_bitand_1_y5),
    .Y6(_8_bitand_1_y6), .Y7(_8_bitand_1_y7), .Y8(_8_bitand_1_y8));
  _8_bitAND _8_bitand_2 (
    .A1(B1), .A2(B2), .A3(B3), .A4(B4), .A5(B5), .A6(B6), .A7(B7), .A8(B8), .B1(not_2_out), .B2(not_2_out),
    .B3(not_2_out), .B4(not_2_out), .B5(not_2_out), .B6(not_2_out), .B7(not_2_out), .B8(not_2_out),
    .Y1(_8_bitand_2_y1), .Y2(_8_bitand_2_y2), .Y3(_8_bitand_2_y3), .Y4(_8_bitand_2_y4), .Y5(_8_bitand_2_y5),
    .Y6(_8_bitand_2_y6), .Y7(_8_bitand_2_y7), .Y8(_8_bitand_2_y8));
  _8_bitXOR _8_bitxor_1 (
    .A1(_8_bitand_1_y1), .A2(_8_bitand_1_y2), .A3(_8_bitand_1_y3), .A4(_8_bitand_1_y4), .A5(_8_bitand_1_y5),
    .A6(_8_bitand_1_y6), .A7(_8_bitand_1_y7), .A8(_8_bitand_1_y8), .B1(NA), .B2(NA), .B3(NA), .B4(NA),
    .B5(NA), .B6(NA), .B7(NA), .B8(NA), .Y1(_8_bitxor_1_y1), .Y2(_8_bitxor_1_y2), .Y3(_8_bitxor_1_y3),
    .Y4(_8_bitxor_1_y4), .Y5(_8_bitxor_1_y5), .Y6(_8_bitxor_1_y6), .Y7(_8_bitxor_1_y7), .Y8(_8_bitxor_1_y8));
  _8_bitXOR _8_bitxor_2 (
    .A1(_8_bitand_2_y1), .A2(_8_bitand_2_y2), .A3(_8_bitand_2_y3), .A4(_8_bitand_2_y4), .A5(_8_bitand_2_y5),
    .A6(_8_bitand_2_y6), .A7(_8_bitand_2_y7), .A8(_8_bitand_2_y8), .B1(NB), .B2(NB), .B3(NB), .B4(NB),
    .B5(NB), .B6(NB), .B7(NB), .B8(NB), .Y1(_8_bitxor_2_y1), .Y2(_8_bitxor_2_y2), .Y3(_8_bitxor_2_y3),
    .Y4(_8_bitxor_2_y4), .Y5(_8_bitxor_2_y5), .Y6(_8_bitxor_2_y6), .Y7(_8_bitxor_2_y7), .Y8(_8_bitxor_2_y8));
  _8_bitAND _8_bitand_3 (
    .A1(_8_bitxor_1_y1), .A2(_8_bitxor_1_y2), .A3(_8_bitxor_1_y3), .A4(_8_bitxor_1_y4), .A5(_8_bitxor_1_y5),
    .A6(_8_bitxor_1_y6), .A7(_8_bitxor_1_y7), .A8(_8_bitxor_1_y8), .B1(_8_bitxor_2_y1), .B2(_8_bitxor_2_y2),
    .B3(_8_bitxor_2_y3), .B4(_8_bitxor_2_y4), .B5(_8_bitxor_2_y5), .B6(_8_bitxor_2_y6), .B7(_8_bitxor_2_y7),
    .B8(_8_bitxor_2_y8), .Y1(_8_bitand_3_y1), .Y2(_8_bitand_3_y2), .Y3(_8_bitand_3_y3), .Y4(_8_bitand_3_y4),
    .Y5(_8_bitand_3_y5), .Y6(_8_bitand_3_y6), .Y7(_8_bitand_3_y7), .Y8(_8_bitand_3_y8));
  _8_bit_adder _8_bit_adder_1 (
    .A1(_8_bitxor_1_y1), .A2(_8_bitxor_1_y2), .A3(_8_bitxor_1_y3), .A4(_8_bitxor_1_y4), .A5(_8_bitxor_1_y5),
    .A6(_8_bitxor_1_y6), .A7(_8_bitxor_1_y7), .A8(_8_bitxor_1_y8), .B1(_8_bitxor_2_y1), .B2(_8_bitxor_2_y2),
    .B3(_8_bitxor_2_y3), .B4(_8_bitxor_2_y4), .B5(_8_bitxor_2_y5), .B6(_8_bitxor_2_y6), .B7(_8_bitxor_2_y7),
    .B8(_8_bitxor_2_y8), .cin(1'b0), .Y1(_8_bit_adder_1_y1), .Y2(_8_bit_adder_1_y2), .Y3(_8_bit_adder_1_y3),
    .Y4(_8_bit_adder_1_y4), .Y5(_8_bit_adder_1_y5), .Y6(_8_bit_adder_1_y6), .Y7(_8_bit_adder_1_y7),
    .Y8(_8_bit_adder_1_y8), .cout(of));
  _8x2mux _8x2mux_1 (
    .A1(_8_bitand_3_y1), .A2(_8_bitand_3_y2), .A3(_8_bitand_3_y3), .A4(_8_bitand_3_y4), .A5(_8_bitand_3_y5),
    .A6(_8_bitand_3_y6), .A7(_8_bitand_3_y7), .A8(_8_bitand_3_y8), .B1(_8_bit_adder_1_y1),
    .B2(_8_bit_adder_1_y2), .B3(_8_bit_adder_1_y3), .B4(_8_bit_adder_1_y4), .B5(_8_bit_adder_1_y5),
    .B6(_8_bit_adder_1_y6), .B7(_8_bit_adder_1_y7), .B8(_8_bit_adder_1_y8), .sel(F), .Y1(_8x2mux_1_y1),
    .Y2(_8x2mux_1_y2), .Y3(_8x2mux_1_y3), .Y4(_8x2mux_1_y4), .Y5(_8x2mux_1_y5), .Y6(_8x2mux_1_y6),
    .Y7(_8x2mux_1_y7), .Y8(_8x2mux_1_y8));
  _8_bitXOR _8_bitxor_3 (
    .A1(_8x2mux_1_y1), .A2(_8x2mux_1_y2), .A3(_8x2mux_1_y3), .A4(_8x2mux_1_y4), .A5(_8x2mux_1_y5),
    .A6(_8x2mux_1_y6), .A7(_8x2mux_1_y7), .A8(_8x2mux_1_y8), .B1(NO), .B2(NO), .B3(NO), .B4(NO), .B5(NO),
    .B6(NO), .B7(NO), .B8(NO), .Y1(Y1), .Y2(Y2), .Y3(Y3), .Y4(Y4), .Y5(Y5), .Y6(Y6), .Y7(Y7), .Y8(lz));
  nor nor_1 (z, Y1, Y2, Y3, Y4, Y5, Y6, Y7, lz);

  assign Y8 = lz;
endmodule
