// Digital circuit Bit.dig as structural Verilog
module Bit (
  input  load,
  input  enable,
  input  D,
  input  c,
  input  R,
  output Q
);

  wire and_1_out, and_2_out, d_flipflop_rising_1_q, not_1_out, not_2_out, or_1_out;

  and and_1 (and_1_out, D, load);
  or or_1 (or_1_out, and_2_out, and_1_out);
  and and_2 (and_2_out, d_flipflop_rising_1_q, not_1_out);
  not not_1 (not_1_out, load);
  D_flipflop_rising d_flipflop_rising_1 (.c(c), .D(or_1_out), .R(R), .Q(d_flipflop_rising_1_q));  // open: Q_2
  TransGate transgate_1 (.A(enable), .nA(not_2_out), .out1(d_flipflop_rising_1_q), .out2(Q));
  not not_2 (not_2_out, enable);
endmodule
