// Digital circuit CPU.dig as structural Verilog
module CPU (
  input  in_1,
  input  in_2,
  input  in_3,
  input  in_4,
  input  in_5,
  input  in_6,
  input  in_7,
  input  in_8,
  input  in_9,
  input  clk,
  input  HLT,
  input  ROM_clk
);

  wire _4_bit_counter_1_q1, _4_bit_counter_1_q2, _4_bit_counter_1_q3, _4_bit_counter_2_q1,
       _4_bit_counter_2_q2, _4_bit_counter_2_q3, _4_bit_counter_2_q4, _4_bit_counter_3_rout,
       _4_bit_register_1_q1, _4_bit_register_1_q2, _4_bit_register_1_q3, _4_bit_register_1_q4, _4x2mux_1_y1,
       _4x2mux_1_y2, _4x2mux_1_y3, _4x2mux_1_y4, _8_bit_register_1_q1, _8_bit_register_1_q2,
       _8_bit_register_1_q3, _8_bit_register_1_q4, _8_bit_register_1_q5, _8_bit_register_1_q6,
       _8_bit_register_1_q7, _8_bit_register_1_q8, _8_bit_register_2_q1, _8_bit_register_2_q2,
       _8_bit_register_2_q3, _8_bit_register_2_q4, _8_bit_register_2_q5, _8_bit_register_2_q6,
       _8_bit_register_2_q7, _8_bit_register_2_q8, _8_bit_register_3_q1, _8_bit_register_3_q2,
       _8_bit_register_3_q3, _8_bit_register_3_q4, _8_bit_register_3_q5, _8_bit_register_3_q6,
       _8_bit_register_3_q7, _8_bit_register_3_q8, _8_bit_register_4_q1, _8_bit_register_4_q2,
       _8_bit_register_4_q3, _8_bit_register_4_q4, _8_bit_register_4_q5, _8_bit_register_4_q6,
       _8_bit_register_4_q7, _8_bit_register_4_q8, alu_1_lz, alu_1_of, alu_1_y1, alu_1_y2, alu_1_y3,
       alu_1_y4, alu_1_y5, alu_1_y6, alu_1_y7, alu_1_y8, alu_1_z, ALU_E, and_1_out, and_2_out, and_4_out,
       and_5_out, AR_E, AR_L, BR_L, bussplitter_1_d0, bussplitter_1_d1, bussplitter_1_d2, bussplitter_1_d3,
       bussplitter_1_d4, bussplitter_1_d5, bussplitter_1_d6, bussplitter_1_d7, clk_t, delay_1_out, F, f_lz,
       f_of, f_z, FL, Go_out, HLT_t, IR_E, IR_L, J, MAR_L, NA, NB, NO, not_1_out, not_2_out, not_3_out,
       octal_bus_tranceiver_1_z1, octal_bus_tranceiver_1_z2, octal_bus_tranceiver_1_z3,
       octal_bus_tranceiver_1_z4, octal_bus_tranceiver_1_z5, octal_bus_tranceiver_1_z6,
       octal_bus_tranceiver_1_z7, octal_bus_tranceiver_1_z8, or_1_out, or_2_out, or_3_out, or_4_out, OR_L,
       PC_C, PC_E, PC_L, R, R_W, ram16byte_1_y1, ram16byte_1_y2, ram16byte_1_y3, ram16byte_1_y4,
       ram16byte_1_y5, ram16byte_1_y6, ram16byte_1_y7, ram16byte_1_y8, RAM_E, ROM_A1, ROM_A2, ROM_A3, ROM_A4,
       ROM_active, ROM_clk_t, Step_out, ZA, ZB;
  wire [3:0] bussplitter_2_d;
  wire [7:0] bussplitter_1_d;

  and and_1 (and_1_out, _4_bit_counter_1_q1, _4_bit_counter_1_q3);
  not not_1 (not_1_out, ROM_active);
  or or_1 (or_1_out, R, and_1_out);
  _4_Bit_Counter _4_bit_counter_1 (
    .L(1'b0), .CE(not_1_out), .clk(not_2_out), .R(or_1_out), .D1(1'b0), .D2(1'b0), .D3(1'b0), .D4(1'b0),
    .Q3(_4_bit_counter_1_q3), .Q2(_4_bit_counter_1_q2), .Q1(_4_bit_counter_1_q1));  // open: rout, Q4
  not not_2 (not_2_out, clk_t);
  LED led_1 (.in(_4_bit_counter_1_q3));
  LED led_2 (.in(_4_bit_counter_1_q1));
  LED led_3 (.in(_4_bit_counter_1_q2));
  SAP_1_LOGIC_UNIT sap_1_logic_unit_1 (
    .I_4(_8_bit_register_1_q1), .I_3(_8_bit_register_1_q2), .I_2(_8_bit_register_1_q3),
    .I_1(_8_bit_register_1_q4), .T_1(_4_bit_counter_1_q1), .T_2(_4_bit_counter_1_q2),
    .T_3(_4_bit_counter_1_q3), .f_lz(f_lz), .f_of(f_of), .f_z(f_z), .PC_C(PC_C), .PC_L(PC_L), .PC_E(PC_E),
    .AR_L(AR_L), .AR_E(AR_E), .BR_L(BR_L), .ALU_E(ALU_E), .NA(NA), .NB(NB), .ZA(ZA), .ZB(ZB), .F(F), .NO(NO),
    .MAR_L(MAR_L), .R_W(R_W), .RAM_E(RAM_E), .IR_L(IR_L), .IR_E(IR_E), .OR_L(OR_L), .J(J), .FL(FL),
    .HLT(HLT_t), .e(delay_1_out));
  Delay #(.delayTime(5)) delay_1 (.in(_4_bit_counter_3_rout), .out(delay_1_out));
  _4x2mux _4x2mux_1 (
    .A1(_4_bit_register_1_q4), .A2(_4_bit_register_1_q3), .A3(_4_bit_register_1_q2),
    .A4(_4_bit_register_1_q1), .B1(ROM_A1), .B2(ROM_A2), .B3(ROM_A3), .B4(ROM_A4), .sel(ROM_active),
    .Y1(_4x2mux_1_y1), .Y2(_4x2mux_1_y2), .Y3(_4x2mux_1_y3), .Y4(_4x2mux_1_y4));
  LED led_4 (.in(_8_bit_register_1_q1));
  _4_Bit_Counter _4_bit_counter_2 (
    .L(PC_L), .CE(PC_C), .clk(clk_t), .R(R), .D1(octal_bus_tranceiver_1_z1), .D2(octal_bus_tranceiver_1_z2),
    .D3(octal_bus_tranceiver_1_z3), .D4(octal_bus_tranceiver_1_z4), .Q4(_4_bit_counter_2_q4),
    .Q3(_4_bit_counter_2_q3), .Q2(_4_bit_counter_2_q2), .Q1(_4_bit_counter_2_q1));  // open: rout
  or or_2 (or_2_out, R_W, ROM_active);
  RAM16Byte ram16byte_1 (
    .R(R), .r_w(or_2_out), .clk(clk_t), .A1(_4x2mux_1_y1), .A2(_4x2mux_1_y2), .A3(_4x2mux_1_y3),
    .A4(_4x2mux_1_y4), .D8(octal_bus_tranceiver_1_z8), .D7(octal_bus_tranceiver_1_z7),
    .D6(octal_bus_tranceiver_1_z6), .D5(octal_bus_tranceiver_1_z5), .D4(octal_bus_tranceiver_1_z4),
    .D3(octal_bus_tranceiver_1_z3), .D2(octal_bus_tranceiver_1_z2), .D1(octal_bus_tranceiver_1_z1),
    .Y1(ram16byte_1_y1), .Y2(ram16byte_1_y2), .Y3(ram16byte_1_y3), .Y4(ram16byte_1_y4), .Y5(ram16byte_1_y5),
    .Y6(ram16byte_1_y6), .Y7(ram16byte_1_y7), .Y8(ram16byte_1_y8));
  Octal_Bus_Tranceiver octal_bus_tranceiver_1 (
    .A1(ram16byte_1_y1), .A2(ram16byte_1_y2), .A3(ram16byte_1_y3), .A4(ram16byte_1_y4), .A5(ram16byte_1_y5),
    .A6(ram16byte_1_y6), .A7(ram16byte_1_y7), .A8(ram16byte_1_y8), .e(RAM_E), .Z1(octal_bus_tranceiver_1_z1),
    .Z2(octal_bus_tranceiver_1_z2), .Z3(octal_bus_tranceiver_1_z3), .Z4(octal_bus_tranceiver_1_z4),
    .Z5(octal_bus_tranceiver_1_z5), .Z6(octal_bus_tranceiver_1_z6), .Z7(octal_bus_tranceiver_1_z7),
    .Z8(octal_bus_tranceiver_1_z8));
  LED led_5 (.in(_8_bit_register_1_q2));
  LED led_6 (.in(_8_bit_register_1_q3));
  LED led_7 (.in(_8_bit_register_1_q4));
  _4_Bit_Register _4_bit_register_1 (
    .load(MAR_L), .c(clk_t), .R(R), .D1(octal_bus_tranceiver_1_z4), .D2(octal_bus_tranceiver_1_z3),
    .D3(octal_bus_tranceiver_1_z2), .D4(octal_bus_tranceiver_1_z1), .Q1(_4_bit_register_1_q1),
    .Q2(_4_bit_register_1_q2), .Q3(_4_bit_register_1_q3), .Q4(_4_bit_register_1_q4));
  Octal_Bus_Tranceiver octal_bus_tranceiver_2 (
    .A1(_4_bit_counter_2_q1), .A2(_4_bit_counter_2_q2), .A3(_4_bit_counter_2_q3), .A4(_4_bit_counter_2_q4),
    .A5(1'b0), .A6(1'b0), .A7(1'b0), .A8(1'b0), .e(PC_E), .Z1(octal_bus_tranceiver_1_z1),
    .Z2(octal_bus_tranceiver_1_z2), .Z3(octal_bus_tranceiver_1_z3), .Z4(octal_bus_tranceiver_1_z4),
    .Z5(octal_bus_tranceiver_1_z5), .Z6(octal_bus_tranceiver_1_z6), .Z7(octal_bus_tranceiver_1_z7),
    .Z8(octal_bus_tranceiver_1_z8));
  _8_bit_register _8_bit_register_1 (
    .D1(octal_bus_tranceiver_1_z8), .D2(octal_bus_tranceiver_1_z7), .D3(octal_bus_tranceiver_1_z6),
    .D4(octal_bus_tranceiver_1_z5), .D5(octal_bus_tranceiver_1_z4), .D6(octal_bus_tranceiver_1_z3),
    .D7(octal_bus_tranceiver_1_z2), .D8(octal_bus_tranceiver_1_z1), .l(IR_L), .c(clk_t), .R(R),
    .Q1(_8_bit_register_1_q1), .Q2(_8_bit_register_1_q2), .Q3(_8_bit_register_1_q3),
    .Q4(_8_bit_register_1_q4), .Q5(_8_bit_register_1_q5), .Q6(_8_bit_register_1_q6),
    .Q7(_8_bit_register_1_q7), .Q8(_8_bit_register_1_q8));
  Octal_Bus_Tranceiver octal_bus_tranceiver_3 (
    .A1(_8_bit_register_1_q8), .A2(_8_bit_register_1_q7), .A3(_8_bit_register_1_q6),
    .A4(_8_bit_register_1_q5), .A5(1'b0), .A6(1'b0), .A7(1'b0), .A8(1'b0), .e(IR_E),
    .Z1(octal_bus_tranceiver_1_z1), .Z2(octal_bus_tranceiver_1_z2), .Z3(octal_bus_tranceiver_1_z3),
    .Z4(octal_bus_tranceiver_1_z4), .Z5(octal_bus_tranceiver_1_z5), .Z6(octal_bus_tranceiver_1_z6),
    .Z7(octal_bus_tranceiver_1_z7), .Z8(octal_bus_tranceiver_1_z8));
  LED led_8 (.in(octal_bus_tranceiver_1_z7));
  LED led_9 (.in(octal_bus_tranceiver_1_z6));
  LED led_10 (.in(octal_bus_tranceiver_1_z5));
  LED led_11 (.in(octal_bus_tranceiver_1_z8));
  Octal_Bus_Tranceiver octal_bus_tranceiver_4 (
    .A1(in_8), .A2(in_7), .A3(in_6), .A4(in_5), .A5(in_4), .A6(in_3), .A7(in_2), .A8(in_1), .e(in_9),
    .Z1(octal_bus_tranceiver_1_z1), .Z2(octal_bus_tranceiver_1_z2), .Z3(octal_bus_tranceiver_1_z3),
    .Z4(octal_bus_tranceiver_1_z4), .Z5(octal_bus_tranceiver_1_z5), .Z6(octal_bus_tranceiver_1_z6),
    .Z7(octal_bus_tranceiver_1_z7), .Z8(octal_bus_tranceiver_1_z8));
  LED led_12 (.in(octal_bus_tranceiver_1_z4));
  LED led_13 (.in(octal_bus_tranceiver_1_z2));
  LED led_14 (.in(octal_bus_tranceiver_1_z1));
  LED led_15 (.in(octal_bus_tranceiver_1_z3));
  Octal_Bus_Tranceiver octal_bus_tranceiver_5 (
    .A1(_8_bit_register_4_q8), .A2(_8_bit_register_4_q7), .A3(_8_bit_register_4_q6),
    .A4(_8_bit_register_4_q5), .A5(_8_bit_register_4_q4), .A6(_8_bit_register_4_q3),
    .A7(_8_bit_register_4_q2), .A8(_8_bit_register_4_q1), .e(AR_E), .Z1(octal_bus_tranceiver_1_z8),
    .Z2(octal_bus_tranceiver_1_z7), .Z3(octal_bus_tranceiver_1_z6), .Z4(octal_bus_tranceiver_1_z5),
    .Z5(octal_bus_tranceiver_1_z4), .Z6(octal_bus_tranceiver_1_z3), .Z7(octal_bus_tranceiver_1_z2),
    .Z8(octal_bus_tranceiver_1_z1));
  Octal_Bus_Tranceiver octal_bus_tranceiver_6 (
    .A1(alu_1_y8), .A2(alu_1_y7), .A3(alu_1_y6), .A4(alu_1_y5), .A5(alu_1_y4), .A6(alu_1_y3), .A7(alu_1_y2),
    .A8(alu_1_y1), .e(ALU_E), .Z1(octal_bus_tranceiver_1_z8), .Z2(octal_bus_tranceiver_1_z7),
    .Z3(octal_bus_tranceiver_1_z6), .Z4(octal_bus_tranceiver_1_z5), .Z5(octal_bus_tranceiver_1_z4),
    .Z6(octal_bus_tranceiver_1_z3), .Z7(octal_bus_tranceiver_1_z2), .Z8(octal_bus_tranceiver_1_z1));
  _8_bit_register _8_bit_register_2 (
    .D1(octal_bus_tranceiver_1_z1), .D2(octal_bus_tranceiver_1_z2), .D3(octal_bus_tranceiver_1_z3),
    .D4(octal_bus_tranceiver_1_z4), .D5(octal_bus_tranceiver_1_z5), .D6(octal_bus_tranceiver_1_z6),
    .D7(octal_bus_tranceiver_1_z7), .D8(octal_bus_tranceiver_1_z8), .l(BR_L), .c(clk_t), .R(R),
    .Q1(_8_bit_register_2_q1), .Q2(_8_bit_register_2_q2), .Q3(_8_bit_register_2_q3),
    .Q4(_8_bit_register_2_q4), .Q5(_8_bit_register_2_q5), .Q6(_8_bit_register_2_q6),
    .Q7(_8_bit_register_2_q7), .Q8(_8_bit_register_2_q8));
  _8_bit_register _8_bit_register_3 (
    .D1(octal_bus_tranceiver_1_z1), .D2(octal_bus_tranceiver_1_z2), .D3(octal_bus_tranceiver_1_z3),
    .D4(octal_bus_tranceiver_1_z4), .D5(octal_bus_tranceiver_1_z5), .D6(octal_bus_tranceiver_1_z6),
    .D7(octal_bus_tranceiver_1_z7), .D8(octal_bus_tranceiver_1_z8), .l(OR_L), .c(clk_t), .R(R),
    .Q1(_8_bit_register_3_q1), .Q2(_8_bit_register_3_q2), .Q3(_8_bit_register_3_q3),
    .Q4(_8_bit_register_3_q4), .Q5(_8_bit_register_3_q5), .Q6(_8_bit_register_3_q6),
    .Q7(_8_bit_register_3_q7), .Q8(_8_bit_register_3_q8));
  not not_3 (not_3_out, _4_bit_counter_3_rout);
  Octal_Bus_Tranceiver octal_bus_tranceiver_7 (
    .A1(bussplitter_1_d7), .A2(bussplitter_1_d6), .A3(bussplitter_1_d5), .A4(bussplitter_1_d4),
    .A5(bussplitter_1_d3), .A6(bussplitter_1_d2), .A7(bussplitter_1_d1), .A8(bussplitter_1_d0),
    .e(and_2_out), .Z1(octal_bus_tranceiver_1_z8), .Z2(octal_bus_tranceiver_1_z7),
    .Z3(octal_bus_tranceiver_1_z6), .Z4(octal_bus_tranceiver_1_z5), .Z5(octal_bus_tranceiver_1_z4),
    .Z6(octal_bus_tranceiver_1_z3), .Z7(octal_bus_tranceiver_1_z2), .Z8(octal_bus_tranceiver_1_z1));
  _8_bit_register _8_bit_register_4 (
    .D1(octal_bus_tranceiver_1_z1), .D2(octal_bus_tranceiver_1_z2), .D3(octal_bus_tranceiver_1_z3),
    .D4(octal_bus_tranceiver_1_z4), .D5(octal_bus_tranceiver_1_z5), .D6(octal_bus_tranceiver_1_z6),
    .D7(octal_bus_tranceiver_1_z7), .D8(octal_bus_tranceiver_1_z8), .l(AR_L), .c(clk_t), .R(R),
    .Q1(_8_bit_register_4_q1), .Q2(_8_bit_register_4_q2), .Q3(_8_bit_register_4_q3),
    .Q4(_8_bit_register_4_q4), .Q5(_8_bit_register_4_q5), .Q6(_8_bit_register_4_q6),
    .Q7(_8_bit_register_4_q7), .Q8(_8_bit_register_4_q8));
  ALU alu_1 (
    .lz(alu_1_lz), .z(alu_1_z), .of(alu_1_of), .NA(NA), .NB(NB), .ZA(ZA), .ZB(ZB), .F(F), .NO(NO),
    .A1(_8_bit_register_4_q1), .A2(_8_bit_register_4_q2), .A3(_8_bit_register_4_q3),
    .A4(_8_bit_register_4_q4), .A5(_8_bit_register_4_q5), .A6(_8_bit_register_4_q6),
    .A7(_8_bit_register_4_q7), .A8(_8_bit_register_4_q8), .B1(_8_bit_register_2_q1),
    .B2(_8_bit_register_2_q2), .B3(_8_bit_register_2_q3), .B4(_8_bit_register_2_q4),
    .B5(_8_bit_register_2_q5), .B6(_8_bit_register_2_q6), .B7(_8_bit_register_2_q7),
    .B8(_8_bit_register_2_q8), .Y1(alu_1_y1), .Y2(alu_1_y2), .Y3(alu_1_y3), .Y4(alu_1_y4), .Y5(alu_1_y5),
    .Y6(alu_1_y6), .Y7(alu_1_y7), .Y8(alu_1_y8));
  LED led_16 (.in(_8_bit_register_3_q7));
  LED led_17 (.in(_8_bit_register_3_q6));
  LED led_18 (.in(_8_bit_register_3_q8));
  and and_2 (and_2_out, ROM_active, not_3_out);
  BusSplitter #(.Bits(8)) bussplitter_1 (
    .D(bussplitter_1_d), .OE(1'b1), .D0(bussplitter_1_d0), .D1(bussplitter_1_d1), .D2(bussplitter_1_d2),
    .D3(bussplitter_1_d3), .D4(bussplitter_1_d4), .D5(bussplitter_1_d5), .D6(bussplitter_1_d6),
    .D7(bussplitter_1_d7));
  LED led_19 (.in(_8_bit_register_3_q5));
  LED led_20 (.in(_8_bit_register_3_q4));
  LED led_21 (.in(_8_bit_register_3_q2));
  LED led_22 (.in(_8_bit_register_3_q3));
  ROM #(.AddrBits(4), .Bits(8)) count_up (.A(bussplitter_2_d), .sel(1'b1), .D(bussplitter_1_d));
  BusSplitter #(.Bits(4)) bussplitter_2 (
    .D(bussplitter_2_d), .OE(1'b0), .D0(ROM_A1), .D1(ROM_A2), .D2(ROM_A3), .D3(ROM_A4));
  LED led_23 (.in(_8_bit_register_4_q7));
  LED led_24 (.in(_8_bit_register_4_q8));
  LED led_25 (.in(_8_bit_register_2_q7));
  LED led_26 (.in(_8_bit_register_2_q8));
  LED led_27 (.in(_8_bit_register_3_q1));
  _4_Bit_Counter _4_bit_counter_3 (
    .L(1'b0), .CE(ROM_active), .clk(ROM_clk_t), .R(R), .D1(1'b0), .D2(1'b0), .D3(1'b0), .D4(1'b0),
    .rout(_4_bit_counter_3_rout), .Q4(ROM_A4), .Q3(ROM_A3), .Q2(ROM_A2), .Q1(ROM_A1));
  LED led_28 (.in(_8_bit_register_4_q6));
  LED led_29 (.in(_8_bit_register_4_q5));
  LED led_30 (.in(_8_bit_register_4_q4));
  LED led_31 (.in(_8_bit_register_4_q3));
  LED led_32 (.in(_8_bit_register_2_q3));
  LED led_33 (.in(_8_bit_register_2_q4));
  LED led_34 (.in(_8_bit_register_2_q5));
  LED led_35 (.in(_8_bit_register_2_q6));
  LED led_36 (.in(_8_bit_register_4_q2));
  LED led_37 (.in(_8_bit_register_4_q1));
  _4_Bit_Register _4_bit_register_2 (
    .load(FL), .c(clk_t), .R(R), .D1(alu_1_lz), .D2(alu_1_z), .D3(alu_1_of), .D4(1'b0), .Q1(f_lz), .Q2(f_z),
    .Q3(f_of));  // open: Q4
  LED led_38 (.in(_8_bit_register_2_q2));
  LED led_39 (.in(_8_bit_register_2_q1));
  and and_3 (ROM_clk_t, ROM_clk, ~_4_bit_counter_3_rout, ROM_active);  // And
  LED led_40 (.in(f_z));
  Button Load_Program (.out(ROM_active));
  LED led_41 (.in(f_lz));
  LED led_42 (.in(f_of));
  Button Reset (.out(R));
  Button Go (.out(Go_out));
  Button Step (.out(Step_out));
  or or_3 (or_3_out, HLT, HLT_t);
  and and_4 (and_4_out, clk, Go_out);
  or or_4 (or_4_out, and_4_out, Step_out);
  and and_5 (and_5_out, or_4_out, ~or_3_out, _4_bit_counter_3_rout);  // And
  or or_5 (clk_t, and_5_out, ROM_clk_t);

  // Notes on the sheet:
  //   clk: Hz: 100
  //   ROM_clk: Hz: 600
  //   0000 LDA
  //   0001 LIA
  //   0010 LDB
  //   0011 LIB
  //   0100 ADD
  //   0101 SUB
  //   0110 INC
  //   0111 DEC
  //   1000 OUT
  //   1001 STA
  //   1010 STB
  //   1011 JZ
  //   1100 JC
  //   1101 JLZ
  //   1110 JMP
  //   1111 HLT
  //   Program Counter
  //   RAM
  //   Memory Address Register
  //   Bus Manual Input
  //   A Register
  //   B Register
  //   contents of count_up (hex, n*v repeats v):
  //   33,40,80,e1,f0,9*0,a,2
  //   ALU
  //   Flag Register
endmodule
