// Digital circuit Comparator.dig as structural Verilog
module Comparator (
  input  B4,
  input  B3,
  input  B2,
  input  B1,
  input  A4,
  input  A3,
  input  A2,
  input  A1,
  output A_eq_B,
  output A__gt__B
);

  wire and_1_out, and_2_out, and_3_out, and_4_out, not_1_out, not_2_out, not_3_out, not_4_out, not_5_out,
       not_6_out, not_7_out;

  and and_1 (and_1_out, A4, not_1_out);
  not not_1 (not_1_out, B4);
  and and_2 (and_2_out, A3, not_5_out, not_2_out);
  not not_2 (not_2_out, B3);
  and and_3 (and_3_out, A3, not_6_out, not_3_out);
  not not_3 (not_3_out, B2);
  and and_4 (and_4_out, A1, not_7_out, not_4_out);
  not not_4 (not_4_out, B1);
  not not_5 (not_5_out, and_1_out);
  not not_6 (not_6_out, and_2_out);
  not not_7 (not_7_out, and_3_out);
  Equals equals_1 (.B4(B4), .B3(B3), .B2(B2), .B1(B1), .A4(A4), .A3(A3), .A2(A2), .A1(A1), .eq(A_eq_B));
  or or_1 (A__gt__B, and_1_out, and_2_out, and_3_out, and_4_out);
endmodule
