// Digital circuit D-flipflop-rising.dig as structural Verilog
module D_flipflop_rising (
  input  c,
  input  D,
  input  R,
  output Q,
  output Q_2
);

  wire d_flipflop_1_q, not_1_out;

  not not_1 (not_1_out, c);
  D_flipflop d_flipflop_1 (.c(not_1_out), .D(D), .P(1'b0), .R(R), .Q(d_flipflop_1_q));  // open: Q_2
  D_flipflop d_flipflop_2 (.c(c), .D(d_flipflop_1_q), .P(1'b0), .R(R), .Q(Q), .Q_2(Q_2));
endmodule
