// Digital circuit D-flipflop.dig as structural Verilog
module D_flipflop (
  input  c,
  input  D,
  input  P,
  input  R,
  output Q,
  output Q_2
);

  wire and_1_out, and_2_out, not_1_out, or_1_out, or_2_out;

  and and_1 (and_1_out, not_1_out, c);
  not not_1 (not_1_out, D);
  and and_2 (and_2_out, D, c);
  or or_1 (or_1_out, R, and_1_out);
  or or_2 (or_2_out, and_2_out, P);
  nor nor_1 (Q, or_1_out, Q_2);
  nor nor_2 (Q_2, Q, or_2_out);
endmodule
