// Digital circuit Equals.dig as structural Verilog
module Equals (
  input  B4,
  input  B3,
  input  B2,
  input  B1,
  input  A4,
  input  A3,
  input  A2,
  input  A1,
  output eq
);

  wire xor_1_out, xor_2_out, xor_3_out, xor_4_out;

  xor xor_1 (xor_1_out, A4, B4);
  xor xor_2 (xor_2_out, A3, B3);
  xor xor_3 (xor_3_out, A2, B2);
  xor xor_4 (xor_4_out, A1, B1);
  nor nor_1 (eq, xor_1_out, xor_2_out, xor_3_out, xor_4_out);
endmodule
