// Digital circuit Full-Adder.dig as structural Verilog
module Full_Adder (
  input  a,
  input  b,
  input  cin,
  output sum,
  output cout
);

  wire half_adder_1_cout, half_adder_1_sum, half_adder_2_cout;

  Half_Adder half_adder_1 (.a(b), .b(cin), .cout(half_adder_1_cout), .sum(half_adder_1_sum));
  Half_Adder half_adder_2 (.a(a), .b(half_adder_1_sum), .cout(half_adder_2_cout), .sum(sum));
  or or_1 (cout, half_adder_1_cout, half_adder_2_cout);
endmodule
