// Digital circuit Octal-Bus-Tranceiver.dig as structural Verilog
module Octal_Bus_Tranceiver (
  input  A1,
  input  A2,
  input  A3,
  input  A4,
  input  A5,
  input  A6,
  input  A7,
  input  A8,
  input  e,
  output Z1,
  output Z2,
  output Z3,
  output Z4,
  output Z5,
  output Z6,
  output Z7,
  output Z8
);

  wire not_1_out;

  TransGate transgate_1 (.A(e), .nA(not_1_out), .out1(A2), .out2(Z2));
  TransGate transgate_2 (.A(e), .nA(not_1_out), .out1(A1), .out2(Z1));
  TransGate transgate_3 (.A(e), .nA(not_1_out), .out1(A4), .out2(Z4));
  TransGate transgate_4 (.A(e), .nA(not_1_out), .out1(A3), .out2(Z3));
  TransGate transgate_5 (.A(e), .nA(not_1_out), .out1(A6), .out2(Z6));
  TransGate transgate_6 (.A(e), .nA(not_1_out), .out1(A5), .out2(Z5));
  TransGate transgate_7 (.A(e), .nA(not_1_out), .out1(A8), .out2(Z8));
  TransGate transgate_8 (.A(e), .nA(not_1_out), .out1(A7), .out2(Z7));
  not not_1 (not_1_out, e);

  // Other names for the same wires on the sheet: aa5 = Z5
endmodule
