// Digital circuit RAM16Byte.dig as structural Verilog
module RAM16Byte (
  input  A1,
  input  A2,
  input  A3,
  input  A4,
  input  D1,
  input  D2,
  input  D3,
  input  D4,
  input  D5,
  input  D6,
  input  D7,
  input  D8,
  input  r_w,
  input  clk,
  input  R,
  output Y1,
  output Y2,
  output Y3,
  output Y4,
  output Y5,
  output Y6,
  output Y7,
  output Y8
);

  wire _0, _1, _2, _3, _4, _4_bit_register_1_q1, _4_bit_register_1_q2, _4_bit_register_1_q3,
       _4_bit_register_1_q4, _4_bit_register_2_q1, _4_bit_register_2_q2, _4_bit_register_2_q3,
       _4_bit_register_2_q4, _4_bit_register_3_q1, _4_bit_register_3_q2, _4_bit_register_3_q3,
       _4_bit_register_3_q4, _4_bit_register_4_q1, _4_bit_register_4_q2, _4_bit_register_4_q3,
       _4_bit_register_4_q4, _4_bit_register_5_q1, _4_bit_register_5_q2, _4_bit_register_5_q3,
       _4_bit_register_5_q4, _4_bit_register_6_q1, _4_bit_register_6_q2, _4_bit_register_6_q3,
       _4_bit_register_6_q4, _4_bit_register_7_q1, _4_bit_register_7_q2, _4_bit_register_7_q3,
       _4_bit_register_7_q4, _4_bit_register_8_q1, _4_bit_register_8_q2, _4_bit_register_8_q3,
       _4_bit_register_8_q4, _4_bit_register_9_q1, _4_bit_register_9_q2, _4_bit_register_9_q3,
       _4_bit_register_9_q4, _4_bit_register_10_q1, _4_bit_register_10_q2, _4_bit_register_10_q3,
       _4_bit_register_10_q4, _4_bit_register_11_q1, _4_bit_register_11_q2, _4_bit_register_11_q3,
       _4_bit_register_11_q4, _4_bit_register_12_q1, _4_bit_register_12_q2, _4_bit_register_12_q3,
       _4_bit_register_12_q4, _4_bit_register_13_q1, _4_bit_register_13_q2, _4_bit_register_13_q3,
       _4_bit_register_13_q4, _4_bit_register_14_q1, _4_bit_register_14_q2, _4_bit_register_14_q3,
       _4_bit_register_14_q4, _4_bit_register_15_q1, _4_bit_register_15_q2, _4_bit_register_15_q3,
       _4_bit_register_15_q4, _4_bit_register_16_q1, _4_bit_register_16_q2, _4_bit_register_16_q3,
       _4_bit_register_16_q4, _4_bit_register_17_q1, _4_bit_register_17_q2, _4_bit_register_17_q3,
       _4_bit_register_17_q4, _4_bit_register_18_q1, _4_bit_register_18_q2, _4_bit_register_18_q3,
       _4_bit_register_18_q4, _4_bit_register_19_q1, _4_bit_register_19_q2, _4_bit_register_19_q3,
       _4_bit_register_19_q4, _4_bit_register_20_q1, _4_bit_register_20_q2, _4_bit_register_20_q3,
       _4_bit_register_20_q4, _4_bit_register_21_q1, _4_bit_register_21_q2, _4_bit_register_21_q3,
       _4_bit_register_21_q4, _4_bit_register_22_q1, _4_bit_register_22_q2, _4_bit_register_22_q3,
       _4_bit_register_22_q4, _4_bit_register_23_q1, _4_bit_register_23_q2, _4_bit_register_23_q3,
       _4_bit_register_23_q4, _4_bit_register_24_q1, _4_bit_register_24_q2, _4_bit_register_24_q3,
       _4_bit_register_24_q4, _4_bit_register_25_q1, _4_bit_register_25_q2, _4_bit_register_25_q3,
       _4_bit_register_25_q4, _4_bit_register_26_q1, _4_bit_register_26_q2, _4_bit_register_26_q3,
       _4_bit_register_26_q4, _4_bit_register_27_q1, _4_bit_register_27_q2, _4_bit_register_27_q3,
       _4_bit_register_27_q4, _4_bit_register_28_q1, _4_bit_register_28_q2, _4_bit_register_28_q3,
       _4_bit_register_28_q4, _4_bit_register_29_q1, _4_bit_register_29_q2, _4_bit_register_29_q3,
       _4_bit_register_29_q4, _4_bit_register_30_q1, _4_bit_register_30_q2, _4_bit_register_30_q3,
       _4_bit_register_30_q4, _4_bit_register_31_q1, _4_bit_register_31_q2, _4_bit_register_31_q3,
       _4_bit_register_31_q4, _4_bit_register_32_q1, _4_bit_register_32_q2, _4_bit_register_32_q3,
       _4_bit_register_32_q4, _5, _6, _7, _8, _9, A, and_1_out, and_2_out, and_3_out, and_4_out, and_5_out,
       and_6_out, and_7_out, and_8_out, and_9_out, and_10_out, and_11_out, and_12_out, and_13_out,
       and_14_out, and_15_out, and_16_out, B, C, D, E, F;

  _4_Bit_Dec _4_bit_dec_1 (
    .D4(A4), .D3(A3), .D2(A2), .D1(A1), ._0(_0), ._1(_1), ._2(_2), ._3(_3), ._4(_4), ._5(_5), ._6(_6),
    ._7(_7), ._8(_8), ._9(_9), ._10(A), ._11(B), ._12(C), ._13(D), ._14(E), ._15(F));
  and and_1 (and_1_out, r_w, _0);
  _4_Bit_Register _4_bit_register_1 (
    .load(and_2_out), .c(clk), .R(R), .D1(D5), .D2(D6), .D3(D7), .D4(D8), .Q1(_4_bit_register_1_q1),
    .Q2(_4_bit_register_1_q2), .Q3(_4_bit_register_1_q3), .Q4(_4_bit_register_1_q4));
  and and_2 (and_2_out, r_w, _4);
  _4_Bit_Register _4_bit_register_2 (
    .load(and_3_out), .c(clk), .R(R), .D1(D5), .D2(D6), .D3(D7), .D4(D8), .Q1(_4_bit_register_2_q1),
    .Q2(_4_bit_register_2_q2), .Q3(_4_bit_register_2_q3), .Q4(_4_bit_register_2_q4));
  and and_3 (and_3_out, r_w, _8);
  _4_Bit_Register _4_bit_register_3 (
    .load(and_4_out), .c(clk), .R(R), .D1(D5), .D2(D6), .D3(D7), .D4(D8), .Q1(_4_bit_register_3_q1),
    .Q2(_4_bit_register_3_q2), .Q3(_4_bit_register_3_q3), .Q4(_4_bit_register_3_q4));
  and and_4 (and_4_out, r_w, C);
  _4_Bit_Register _4_bit_register_4 (
    .load(and_1_out), .c(clk), .R(R), .D1(D5), .D2(D6), .D3(D7), .D4(D8), .Q1(_4_bit_register_4_q1),
    .Q2(_4_bit_register_4_q2), .Q3(_4_bit_register_4_q3), .Q4(_4_bit_register_4_q4));
  _4_Bit_Register _4_bit_register_5 (
    .load(and_1_out), .c(clk), .R(R), .D1(D1), .D2(D2), .D3(D3), .D4(D4), .Q1(_4_bit_register_5_q1),
    .Q2(_4_bit_register_5_q2), .Q3(_4_bit_register_5_q3), .Q4(_4_bit_register_5_q4));
  Octal_Bus_Tranceiver octal_bus_tranceiver_1 (
    .A1(_4_bit_register_5_q1), .A2(_4_bit_register_5_q2), .A3(_4_bit_register_5_q3),
    .A4(_4_bit_register_5_q4), .A5(_4_bit_register_4_q1), .A6(_4_bit_register_4_q2),
    .A7(_4_bit_register_4_q3), .A8(_4_bit_register_4_q4), .e(_0), .Z1(Y1), .Z2(Y2), .Z3(Y3), .Z4(Y4),
    .Z5(Y5), .Z6(Y6), .Z7(Y7), .Z8(Y8));
  _4_Bit_Register _4_bit_register_6 (
    .load(and_2_out), .c(clk), .R(R), .D1(D1), .D2(D2), .D3(D3), .D4(D4), .Q1(_4_bit_register_6_q1),
    .Q2(_4_bit_register_6_q2), .Q3(_4_bit_register_6_q3), .Q4(_4_bit_register_6_q4));
  Octal_Bus_Tranceiver octal_bus_tranceiver_2 (
    .A1(_4_bit_register_6_q1), .A2(_4_bit_register_6_q2), .A3(_4_bit_register_6_q3),
    .A4(_4_bit_register_6_q4), .A5(_4_bit_register_1_q1), .A6(_4_bit_register_1_q2),
    .A7(_4_bit_register_1_q3), .A8(_4_bit_register_1_q4), .e(_4), .Z1(Y1), .Z2(Y2), .Z3(Y3), .Z4(Y4),
    .Z5(Y5), .Z6(Y6), .Z7(Y7), .Z8(Y8));
  _4_Bit_Register _4_bit_register_7 (
    .load(and_3_out), .c(clk), .R(R), .D1(D1), .D2(D2), .D3(D3), .D4(D4), .Q1(_4_bit_register_7_q1),
    .Q2(_4_bit_register_7_q2), .Q3(_4_bit_register_7_q3), .Q4(_4_bit_register_7_q4));
  Octal_Bus_Tranceiver octal_bus_tranceiver_3 (
    .A1(_4_bit_register_7_q1), .A2(_4_bit_register_7_q2), .A3(_4_bit_register_7_q3),
    .A4(_4_bit_register_7_q4), .A5(_4_bit_register_2_q1), .A6(_4_bit_register_2_q2),
    .A7(_4_bit_register_2_q3), .A8(_4_bit_register_2_q4), .e(_8), .Z1(Y1), .Z2(Y2), .Z3(Y3), .Z4(Y4),
    .Z5(Y5), .Z6(Y6), .Z7(Y7), .Z8(Y8));
  _4_Bit_Register _4_bit_register_8 (
    .load(and_4_out), .c(clk), .R(R), .D1(D1), .D2(D2), .D3(D3), .D4(D4), .Q1(_4_bit_register_8_q1),
    .Q2(_4_bit_register_8_q2), .Q3(_4_bit_register_8_q3), .Q4(_4_bit_register_8_q4));
  Octal_Bus_Tranceiver octal_bus_tranceiver_4 (
    .A1(_4_bit_register_8_q1), .A2(_4_bit_register_8_q2), .A3(_4_bit_register_8_q3),
    .A4(_4_bit_register_8_q4), .A5(_4_bit_register_3_q1), .A6(_4_bit_register_3_q2),
    .A7(_4_bit_register_3_q3), .A8(_4_bit_register_3_q4), .e(C), .Z1(Y1), .Z2(Y2), .Z3(Y3), .Z4(Y4), .Z5(Y5),
    .Z6(Y6), .Z7(Y7), .Z8(Y8));
  and and_5 (and_5_out, r_w, _1);
  _4_Bit_Register _4_bit_register_9 (
    .load(and_6_out), .c(clk), .R(R), .D1(D5), .D2(D6), .D3(D7), .D4(D8), .Q1(_4_bit_register_9_q1),
    .Q2(_4_bit_register_9_q2), .Q3(_4_bit_register_9_q3), .Q4(_4_bit_register_9_q4));
  and and_6 (and_6_out, r_w, _5);
  _4_Bit_Register _4_bit_register_10 (
    .load(and_7_out), .c(clk), .R(R), .D1(D5), .D2(D6), .D3(D7), .D4(D8), .Q1(_4_bit_register_10_q1),
    .Q2(_4_bit_register_10_q2), .Q3(_4_bit_register_10_q3), .Q4(_4_bit_register_10_q4));
  and and_7 (and_7_out, r_w, _9);
  _4_Bit_Register _4_bit_register_11 (
    .load(and_8_out), .c(clk), .R(R), .D1(D5), .D2(D6), .D3(D7), .D4(D8), .Q1(_4_bit_register_11_q1),
    .Q2(_4_bit_register_11_q2), .Q3(_4_bit_register_11_q3), .Q4(_4_bit_register_11_q4));
  and and_8 (and_8_out, r_w, D);
  _4_Bit_Register _4_bit_register_12 (
    .load(and_5_out), .c(clk), .R(R), .D1(D5), .D2(D6), .D3(D7), .D4(D8), .Q1(_4_bit_register_12_q1),
    .Q2(_4_bit_register_12_q2), .Q3(_4_bit_register_12_q3), .Q4(_4_bit_register_12_q4));
  _4_Bit_Register _4_bit_register_13 (
    .load(and_5_out), .c(clk), .R(R), .D1(D1), .D2(D2), .D3(D3), .D4(D4), .Q1(_4_bit_register_13_q1),
    .Q2(_4_bit_register_13_q2), .Q3(_4_bit_register_13_q3), .Q4(_4_bit_register_13_q4));
  Octal_Bus_Tranceiver octal_bus_tranceiver_5 (
    .A1(_4_bit_register_13_q1), .A2(_4_bit_register_13_q2), .A3(_4_bit_register_13_q3),
    .A4(_4_bit_register_13_q4), .A5(_4_bit_register_12_q1), .A6(_4_bit_register_12_q2),
    .A7(_4_bit_register_12_q3), .A8(_4_bit_register_12_q4), .e(_1), .Z1(Y1), .Z2(Y2), .Z3(Y3), .Z4(Y4),
    .Z5(Y5), .Z6(Y6), .Z7(Y7), .Z8(Y8));
  _4_Bit_Register _4_bit_register_14 (
    .load(and_6_out), .c(clk), .R(R), .D1(D1), .D2(D2), .D3(D3), .D4(D4), .Q1(_4_bit_register_14_q1),
    .Q2(_4_bit_register_14_q2), .Q3(_4_bit_register_14_q3), .Q4(_4_bit_register_14_q4));
  Octal_Bus_Tranceiver octal_bus_tranceiver_6 (
    .A1(_4_bit_register_14_q1), .A2(_4_bit_register_14_q2), .A3(_4_bit_register_14_q3),
    .A4(_4_bit_register_14_q4), .A5(_4_bit_register_9_q1), .A6(_4_bit_register_9_q2),
    .A7(_4_bit_register_9_q3), .A8(_4_bit_register_9_q4), .e(_5), .Z1(Y1), .Z2(Y2), .Z3(Y3), .Z4(Y4),
    .Z5(Y5), .Z6(Y6), .Z7(Y7), .Z8(Y8));
  _4_Bit_Register _4_bit_register_15 (
    .load(and_7_out), .c(clk), .R(R), .D1(D1), .D2(D2), .D3(D3), .D4(D4), .Q1(_4_bit_register_15_q1),
    .Q2(_4_bit_register_15_q2), .Q3(_4_bit_register_15_q3), .Q4(_4_bit_register_15_q4));
  Octal_Bus_Tranceiver octal_bus_tranceiver_7 (
    .A1(_4_bit_register_15_q1), .A2(_4_bit_register_15_q2), .A3(_4_bit_register_15_q3),
    .A4(_4_bit_register_15_q4), .A5(_4_bit_register_10_q1), .A6(_4_bit_register_10_q2),
    .A7(_4_bit_register_10_q3), .A8(_4_bit_register_10_q4), .e(_9), .Z1(Y1), .Z2(Y2), .Z3(Y3), .Z4(Y4),
    .Z5(Y5), .Z6(Y6), .Z7(Y7), .Z8(Y8));
  _4_Bit_Register _4_bit_register_16 (
    .load(and_8_out), .c(clk), .R(R), .D1(D1), .D2(D2), .D3(D3), .D4(D4), .Q1(_4_bit_register_16_q1),
    .Q2(_4_bit_register_16_q2), .Q3(_4_bit_register_16_q3), .Q4(_4_bit_register_16_q4));
  Octal_Bus_Tranceiver octal_bus_tranceiver_8 (
    .A1(_4_bit_register_16_q1), .A2(_4_bit_register_16_q2), .A3(_4_bit_register_16_q3),
    .A4(_4_bit_register_16_q4), .A5(_4_bit_register_11_q1), .A6(_4_bit_register_11_q2),
    .A7(_4_bit_register_11_q3), .A8(_4_bit_register_11_q4), .e(D), .Z1(Y1), .Z2(Y2), .Z3(Y3), .Z4(Y4),
    .Z5(Y5), .Z6(Y6), .Z7(Y7), .Z8(Y8));
  and and_9 (and_9_out, r_w, E);
  _4_Bit_Register _4_bit_register_17 (
    .load(and_10_out), .c(clk), .R(R), .D1(D5), .D2(D6), .D3(D7), .D4(D8), .Q1(_4_bit_register_17_q1),
    .Q2(_4_bit_register_17_q2), .Q3(_4_bit_register_17_q3), .Q4(_4_bit_register_17_q4));
  and and_10 (and_10_out, r_w, _2);
  _4_Bit_Register _4_bit_register_18 (
    .load(and_11_out), .c(clk), .R(R), .D1(D5), .D2(D6), .D3(D7), .D4(D8), .Q1(_4_bit_register_18_q1),
    .Q2(_4_bit_register_18_q2), .Q3(_4_bit_register_18_q3), .Q4(_4_bit_register_18_q4));
  and and_11 (and_11_out, r_w, _6);
  _4_Bit_Register _4_bit_register_19 (
    .load(and_12_out), .c(clk), .R(R), .D1(D5), .D2(D6), .D3(D7), .D4(D8), .Q1(_4_bit_register_19_q1),
    .Q2(_4_bit_register_19_q2), .Q3(_4_bit_register_19_q3), .Q4(_4_bit_register_19_q4));
  and and_12 (and_12_out, r_w, A);
  _4_Bit_Register _4_bit_register_20 (
    .load(and_9_out), .c(clk), .R(R), .D1(D5), .D2(D6), .D3(D7), .D4(D8), .Q1(_4_bit_register_20_q1),
    .Q2(_4_bit_register_20_q2), .Q3(_4_bit_register_20_q3), .Q4(_4_bit_register_20_q4));
  _4_Bit_Register _4_bit_register_21 (
    .load(and_9_out), .c(clk), .R(R), .D1(D1), .D2(D2), .D3(D3), .D4(D4), .Q1(_4_bit_register_21_q1),
    .Q2(_4_bit_register_21_q2), .Q3(_4_bit_register_21_q3), .Q4(_4_bit_register_21_q4));
  Octal_Bus_Tranceiver octal_bus_tranceiver_9 (
    .A1(_4_bit_register_21_q1), .A2(_4_bit_register_21_q2), .A3(_4_bit_register_21_q3),
    .A4(_4_bit_register_21_q4), .A5(_4_bit_register_20_q1), .A6(_4_bit_register_20_q2),
    .A7(_4_bit_register_20_q3), .A8(_4_bit_register_20_q4), .e(E), .Z1(Y1), .Z2(Y2), .Z3(Y3), .Z4(Y4),
    .Z5(Y5), .Z6(Y6), .Z7(Y7), .Z8(Y8));
  _4_Bit_Register _4_bit_register_22 (
    .load(and_10_out), .c(clk), .R(R), .D1(D1), .D2(D2), .D3(D3), .D4(D4), .Q1(_4_bit_register_22_q1),
    .Q2(_4_bit_register_22_q2), .Q3(_4_bit_register_22_q3), .Q4(_4_bit_register_22_q4));
  Octal_Bus_Tranceiver octal_bus_tranceiver_10 (
    .A1(_4_bit_register_22_q1), .A2(_4_bit_register_22_q2), .A3(_4_bit_register_22_q3),
    .A4(_4_bit_register_22_q4), .A5(_4_bit_register_17_q1), .A6(_4_bit_register_17_q2),
    .A7(_4_bit_register_17_q3), .A8(_4_bit_register_17_q4), .e(_2), .Z1(Y1), .Z2(Y2), .Z3(Y3), .Z4(Y4),
    .Z5(Y5), .Z6(Y6), .Z7(Y7), .Z8(Y8));
  _4_Bit_Register _4_bit_register_23 (
    .load(and_11_out), .c(clk), .R(R), .D1(D1), .D2(D2), .D3(D3), .D4(D4), .Q1(_4_bit_register_23_q1),
    .Q2(_4_bit_register_23_q2), .Q3(_4_bit_register_23_q3), .Q4(_4_bit_register_23_q4));
  Octal_Bus_Tranceiver octal_bus_tranceiver_11 (
    .A1(_4_bit_register_23_q1), .A2(_4_bit_register_23_q2), .A3(_4_bit_register_23_q3),
    .A4(_4_bit_register_23_q4), .A5(_4_bit_register_18_q1), .A6(_4_bit_register_18_q2),
    .A7(_4_bit_register_18_q3), .A8(_4_bit_register_18_q4), .e(_6), .Z1(Y1), .Z2(Y2), .Z3(Y3), .Z4(Y4),
    .Z5(Y5), .Z6(Y6), .Z7(Y7), .Z8(Y8));
  _4_Bit_Register _4_bit_register_24 (
    .load(and_12_out), .c(clk), .R(R), .D1(D1), .D2(D2), .D3(D3), .D4(D4), .Q1(_4_bit_register_24_q1),
    .Q2(_4_bit_register_24_q2), .Q3(_4_bit_register_24_q3), .Q4(_4_bit_register_24_q4));
  Octal_Bus_Tranceiver octal_bus_tranceiver_12 (
    .A1(_4_bit_register_24_q1), .A2(_4_bit_register_24_q2), .A3(_4_bit_register_24_q3),
    .A4(_4_bit_register_24_q4), .A5(_4_bit_register_19_q1), .A6(_4_bit_register_19_q2),
    .A7(_4_bit_register_19_q3), .A8(_4_bit_register_19_q4), .e(A), .Z1(Y1), .Z2(Y2), .Z3(Y3), .Z4(Y4),
    .Z5(Y5), .Z6(Y6), .Z7(Y7), .Z8(Y8));
  and and_13 (and_13_out, r_w, F);
  _4_Bit_Register _4_bit_register_25 (
    .load(and_14_out), .c(clk), .R(R), .D1(D5), .D2(D6), .D3(D7), .D4(D8), .Q1(_4_bit_register_25_q1),
    .Q2(_4_bit_register_25_q2), .Q3(_4_bit_register_25_q3), .Q4(_4_bit_register_25_q4));
  and and_14 (and_14_out, r_w, _3);
  _4_Bit_Register _4_bit_register_26 (
    .load(and_15_out), .c(clk), .R(R), .D1(D5), .D2(D6), .D3(D7), .D4(D8), .Q1(_4_bit_register_26_q1),
    .Q2(_4_bit_register_26_q2), .Q3(_4_bit_register_26_q3), .Q4(_4_bit_register_26_q4));
  and and_15 (and_15_out, r_w, _7);
  _4_Bit_Register _4_bit_register_27 (
    .load(and_16_out), .c(clk), .R(R), .D1(D5), .D2(D6), .D3(D7), .D4(D8), .Q1(_4_bit_register_27_q1),
    .Q2(_4_bit_register_27_q2), .Q3(_4_bit_register_27_q3), .Q4(_4_bit_register_27_q4));
  and and_16 (and_16_out, r_w, B);
  _4_Bit_Register _4_bit_register_28 (
    .load(and_13_out), .c(clk), .R(R), .D1(D5), .D2(D6), .D3(D7), .D4(D8), .Q1(_4_bit_register_28_q1),
    .Q2(_4_bit_register_28_q2), .Q3(_4_bit_register_28_q3), .Q4(_4_bit_register_28_q4));
  _4_Bit_Register _4_bit_register_29 (
    .load(and_13_out), .c(clk), .R(R), .D1(D1), .D2(D2), .D3(D3), .D4(D4), .Q1(_4_bit_register_29_q1),
    .Q2(_4_bit_register_29_q2), .Q3(_4_bit_register_29_q3), .Q4(_4_bit_register_29_q4));
  Octal_Bus_Tranceiver octal_bus_tranceiver_13 (
    .A1(_4_bit_register_29_q1), .A2(_4_bit_register_29_q2), .A3(_4_bit_register_29_q3),
    .A4(_4_bit_register_29_q4), .A5(_4_bit_register_28_q1), .A6(_4_bit_register_28_q2),
    .A7(_4_bit_register_28_q3), .A8(_4_bit_register_28_q4), .e(F), .Z1(Y1), .Z2(Y2), .Z3(Y3), .Z4(Y4),
    .Z5(Y5), .Z6(Y6), .Z7(Y7), .Z8(Y8));
  _4_Bit_Register _4_bit_register_30 (
    .load(and_14_out), .c(clk), .R(R), .D1(D1), .D2(D2), .D3(D3), .D4(D4), .Q1(_4_bit_register_30_q1),
    .Q2(_4_bit_register_30_q2), .Q3(_4_bit_register_30_q3), .Q4(_4_bit_register_30_q4));
  Octal_Bus_Tranceiver octal_bus_tranceiver_14 (
    .A1(_4_bit_register_30_q1), .A2(_4_bit_register_30_q2), .A3(_4_bit_register_30_q3),
    .A4(_4_bit_register_30_q4), .A5(_4_bit_register_25_q1), .A6(_4_bit_register_25_q2),
    .A7(_4_bit_register_25_q3), .A8(_4_bit_register_25_q4), .e(_3), .Z1(Y1), .Z2(Y2), .Z3(Y3), .Z4(Y4),
    .Z5(Y5), .Z6(Y6), .Z7(Y7), .Z8(Y8));
  _4_Bit_Register _4_bit_register_31 (
    .load(and_15_out), .c(clk), .R(R), .D1(D1), .D2(D2), .D3(D3), .D4(D4), .Q1(_4_bit_register_31_q1),
    .Q2(_4_bit_register_31_q2), .Q3(_4_bit_register_31_q3), .Q4(_4_bit_register_31_q4));
  Octal_Bus_Tranceiver octal_bus_tranceiver_15 (
    .A1(_4_bit_register_31_q1), .A2(_4_bit_register_31_q2), .A3(_4_bit_register_31_q3),
    .A4(_4_bit_register_31_q4), .A5(_4_bit_register_26_q1), .A6(_4_bit_register_26_q2),
    .A7(_4_bit_register_26_q3), .A8(_4_bit_register_26_q4), .e(_7), .Z1(Y1), .Z2(Y2), .Z3(Y3), .Z4(Y4),
    .Z5(Y5), .Z6(Y6), .Z7(Y7), .Z8(Y8));
  _4_Bit_Register _4_bit_register_32 (
    .load(and_16_out), .c(clk), .R(R), .D1(D1), .D2(D2), .D3(D3), .D4(D4), .Q1(_4_bit_register_32_q1),
    .Q2(_4_bit_register_32_q2), .Q3(_4_bit_register_32_q3), .Q4(_4_bit_register_32_q4));
  Octal_Bus_Tranceiver octal_bus_tranceiver_16 (
    .A1(_4_bit_register_32_q1), .A2(_4_bit_register_32_q2), .A3(_4_bit_register_32_q3),
    .A4(_4_bit_register_32_q4), .A5(_4_bit_register_27_q1), .A6(_4_bit_register_27_q2),
    .A7(_4_bit_register_27_q3), .A8(_4_bit_register_27_q4), .e(B), .Z1(Y1), .Z2(Y2), .Z3(Y3), .Z4(Y4),
    .Z5(Y5), .Z6(Y6), .Z7(Y7), .Z8(Y8));
endmodule
