// Digital circuit ROM_loader.dig as structural Verilog
module ROM_loader (
  input  B1,
  input  B2,
  input  B3,
  input  B4,
  input  B5,
  input  B6,
  input  B7,
  input  B8
);

  BusSplitter #(.Bits(8)) bussplitter_1 ();  // open: D, OE, D0, D1, D2, D3, D4, D5, D6, D7
endmodule
