// Digital circuit SAP-1_LOGIC_UNIT.dig as structural Verilog
module SAP_1_LOGIC_UNIT (
  input  I_1,
  input  I_2,
  input  I_3,
  input  I_4,
  input  T_1,
  input  T_2,
  input  T_3,
  input  f_z,
  input  f_lz,
  input  f_of,
  input  e,
  output FL,
  output J,
  output OR_L,
  output IR_E,
  output IR_L,
  output RAM_E,
  output R_W,
  output MAR_L,
  output ALU_E,
  output NA,
  output NB,
  output ZA,
  output ZB,
  output F,
  output NO,
  output BR_L,
  output AR_E,
  output AR_L,
  output PC_E,
  output PC_L,
  output PC_C,
  output HLT
);

  wire _4_bit_dec_1__0, _4_bit_dec_1__1, _4_bit_dec_1__2, _4_bit_dec_1__3, _4_bit_dec_1__4, _4_bit_dec_1__5,
       _4_bit_dec_1__6, _4_bit_dec_1__7, _4_bit_dec_1__8, _4_bit_dec_1__9, _4_bit_dec_1__11,
       _4_bit_dec_1__12, _4_bit_dec_1__13, _4_bit_dec_1__14, _4_bit_dec_1__15, _4_bit_dec_2_p1,
       _4_bit_dec_2_p3, _4_bit_dec_2_p5, _4_bit_dec_2_p7, _4_bit_dec_2_p9, and_1_out, and_2_out, and_3_out,
       and_4_out, and_5_out, and_6_out, and_7_out, and_8_out, and_9_out, and_10_out, and_11_out, and_12_out,
       and_13_out, and_14_out, and_15_out, and_16_out, and_17_out, or_1_out, or_2_out, or_3_out, or_4_out,
       or_5_out, or_6_out, or_7_out, or_8_out, or_9_out, or_10_out, or_11_out, or_12_out, or_13_out,
       or_14_out;

  _4_Bit_Dec _4_bit_dec_1 (
    .D4(I_4), .D3(I_3), .D2(I_2), .D1(I_1), ._0(_4_bit_dec_1__0), ._1(_4_bit_dec_1__1), ._2(_4_bit_dec_1__2),
    ._3(_4_bit_dec_1__3), ._4(_4_bit_dec_1__4), ._5(_4_bit_dec_1__5), ._6(_4_bit_dec_1__6),
    ._7(_4_bit_dec_1__7), ._8(_4_bit_dec_1__8), ._9(_4_bit_dec_1__9), ._11(_4_bit_dec_1__11),
    ._12(_4_bit_dec_1__12), ._13(_4_bit_dec_1__13), ._14(_4_bit_dec_1__14), ._15(_4_bit_dec_1__15));  // open: _10
  and and_1 (and_1_out, _4_bit_dec_1__13, f_lz);
  or or_1 (or_1_out, and_5_out, and_2_out, and_1_out, _4_bit_dec_1__14);
  and and_2 (and_2_out, _4_bit_dec_1__12, f_of);
  and and_3 (and_3_out, _4_bit_dec_2_p5, or_1_out);
  and and_4 (and_4_out, _4_bit_dec_2_p1, _4_bit_dec_1__9);
  and and_5 (and_5_out, _4_bit_dec_1__11, f_z);
  and and_6 (and_6_out, _4_bit_dec_2_p5, _4_bit_dec_1__9);
  and and_7 (and_7_out, _4_bit_dec_2_p5, _4_bit_dec_1__8);
  and and_8 (and_8_out, _4_bit_dec_2_p5, _4_bit_dec_1__6);
  and and_9 (and_9_out, _4_bit_dec_2_p5, _4_bit_dec_1__7);
  and and_10 (and_10_out, _4_bit_dec_2_p5, _4_bit_dec_1__5);
  and and_11 (and_11_out, _4_bit_dec_2_p5, _4_bit_dec_1__4);
  and and_12 (and_12_out, _4_bit_dec_2_p3, _4_bit_dec_1__2);
  and and_13 (and_13_out, _4_bit_dec_2_p5, _4_bit_dec_1__3);
  and and_14 (and_14_out, _4_bit_dec_2_p5, _4_bit_dec_1__2);
  and and_15 (and_15_out, _4_bit_dec_2_p5, _4_bit_dec_1__1);
  and and_16 (and_16_out, _4_bit_dec_2_p5, _4_bit_dec_1__0);
  and and_17 (and_17_out, _4_bit_dec_2_p3, _4_bit_dec_1__0);
  // _4_Bit_Dec _4_bit_dec_2: pin names not known; wires that end beside it: _4_bit_dec_2_p1, T_1, _4_bit_dec_2_p3, T_2, _4_bit_dec_2_p5, T_3, _4_bit_dec_2_p7, 1'b0, _4_bit_dec_2_p9
  and and_18 (PC_C, e, _4_bit_dec_2_p7);
  or or_2 (or_2_out, and_17_out, and_11_out, and_9_out, and_9_out, and_15_out, and_10_out, and_8_out);
  or or_3 (or_3_out, and_7_out, and_4_out);
  or or_4 (or_4_out, and_12_out, and_13_out);
  or or_5 (or_5_out, and_11_out, and_8_out, and_10_out, and_9_out);
  or or_6 (or_6_out, and_10_out, and_8_out);
  or or_7 (or_7_out, and_8_out, and_9_out);
  or or_8 (or_8_out, and_8_out, and_9_out);
  or or_9 (or_9_out, and_11_out, and_8_out, and_10_out, and_9_out);
  or or_10 (or_10_out, and_10_out, and_8_out);
  or or_11 (or_11_out, _4_bit_dec_2_p9, and_14_out, and_16_out, and_6_out);
  or or_12 (or_12_out, _4_bit_dec_2_p7, and_12_out, and_17_out);
  or or_13 (or_13_out, and_16_out, and_14_out, and_6_out, and_15_out, and_13_out, and_3_out);
  or or_14 (or_14_out, and_11_out, and_10_out, and_8_out, and_9_out);
  and and_19 (PC_L, e, and_3_out);
  and and_20 (PC_E, _4_bit_dec_2_p9, e);
  and and_21 (AR_L, or_2_out, e);
  and and_22 (AR_E, or_3_out, e);
  and and_23 (BR_L, or_4_out, e);
  and and_24 (ALU_E, or_5_out, e);
  and and_25 (NA, e, or_6_out);
  and and_26 (NB, e, or_7_out);
  and and_27 (ZB, or_8_out, e);
  and and_28 (F, or_9_out, e);
  and and_29 (NO, or_10_out, e);
  and and_30 (MAR_L, e, or_11_out);
  and and_31 (R_W, e, and_4_out);
  and and_32 (RAM_E, or_12_out, e);
  and and_33 (IR_L, _4_bit_dec_2_p7, e);
  and and_34 (IR_E, or_13_out, e);
  and and_35 (OR_L, and_7_out, e);
  and and_36 (J, and_3_out, e);
  and and_37 (FL, or_14_out, e);
  and and_38 (HLT, _4_bit_dec_1__15, e);

  assign ZA = 1'b0;

  // Notes on the sheet:
  //   0000 LDA
  //   0001 LIA
  //   0010 LDB
  //   0011 LIB
  //   0100 ADD
  //   0101 SUB
  //   0110 INC
  //   0111 DEC
  //   1000 OUT
  //   1001 STA
  //   1010 
  //   1011 JZ
  //   1100 JC
  //   1101 JLZ
  //   1110 JMP
  //   1111 HLT
  //   JLZ
  //   JC
  //   JMP
  //   JZ
  //   STA
  //   OUT
  //   DEC
  //   INC
  //   ADD
  //   SUB
  //   LIB
  //   LDB
  //   LIA
  //   LDA
  //   T0, T1 Fetch cycle
endmodule
