// Digital circuit count.dig as structural Verilog
module count (
  input  clk,
  input  in_2,
  input  in_3
);

  wire _4_bit_simple_counter_1_q1, _4_bit_simple_counter_1_q2, _4_bit_simple_counter_1_q3,
       _4_bit_simple_counter_1_q4, _7seg_driver_1_t1, _7seg_driver_1_t2, _7seg_driver_1_t3,
       _7seg_driver_1_u1, _7seg_driver_1_u2, _7seg_driver_1_u3, _7seg_driver_1_u4;

  _4_bit_simple_counter _4_bit_simple_counter_1 (
    .R(in_2), .CE(in_3), .clk(clk), .Q1(_4_bit_simple_counter_1_q1), .Q2(_4_bit_simple_counter_1_q2),
    .Q3(_4_bit_simple_counter_1_q3), .Q4(_4_bit_simple_counter_1_q4));  // open: rout
  _7seg_driver _7seg_driver_1 (
    .D1(_4_bit_simple_counter_1_q4), .D2(_4_bit_simple_counter_1_q3), .D3(_4_bit_simple_counter_1_q2),
    .D4(_4_bit_simple_counter_1_q1), .t1(_7seg_driver_1_t1), .t2(_7seg_driver_1_t2), .t3(_7seg_driver_1_t3),
    .u1(_7seg_driver_1_u1), .u2(_7seg_driver_1_u2), .u3(_7seg_driver_1_u3), .u4(_7seg_driver_1_u4));
  Seven_Seg seven_seg_1 (
    .a(_7seg_driver_1_u1), .b(_7seg_driver_1_u2), .c(_7seg_driver_1_u3), .d(_7seg_driver_1_u4),
    .e(_7seg_driver_1_t1), .f(_7seg_driver_1_t2), .g(_7seg_driver_1_t3), .dp(1'b0));

  // Notes on the sheet:
  //   clk: Hz: 5
endmodule
