// Digital circuit demux.dig as structural Verilog
module demux (
  input  in,
  input  sel,
  output Y2,
  output Y1
);

  wire not_1_out;

  not not_1 (not_1_out, sel);
  and and_1 (Y2, in, sel);
  and and_2 (Y1, in, not_1_out);
endmodule
